# Fritzing sketch DIY_Arduino_Synteny_V2 (saved by Fritzing 0.8.7b)
circuit board: 2.78084cm x 6.18635cm
breadboards: 1

parts:
  U1 = atmega328 [package=dip]
  Y1 = Resonator [frequency="16 Mhz" package=THT]
  U2 = Voltage Regulator - 5V [package="TO220 [THT]"]
  C1 = Capacitor [part_number=.1uF package=cap-pth-small2]
  LED1 = LED - 5mm [color="Red (633nm)" package="5 mm [THT]"]
  R1 = Resistor [tolerance=±5% resistance=220 package=THT]
  Power_plug1 = Power plug
  J16 = female pin header, 2 pins [form="♀ (female)"]
  J10 = female pin header, 6 pins [form="♀ (female)"]
  J13 = female pin header, 4 pins [form="♀ (female)"]
  J11 = female pin header, 5 pins [form="♀ (female)"]
  J12 = female pin header, 5 pins [form="♀ (female)"]
  J15 = female pin header, 2 pins [form="♀ (female)"]
  J15_2 = female pin header, 2 pins [form="♀ (female)"]
  J9 = female pin header, 2 pins [form="♀ (female)"]
  J14 = female pin header, 2 pins [form="♀ (female)"]

nets:
  GND: U1.RESET, U1.GND, Y1.GND, U2.GND, C1.2, R1.Pin_0, Power_plug1.GND, J16.pin1, J9.pin1, J14.pin1
  N1: U1.D0_(RX), J12.pin1, J15.pin1, J15_2.pin1
  N2: U1.D1_(TX), J12.pin2, J15.pin2, J15_2.pin2
  N3: U1.D2, J12.pin3
  N4: U1.D3_(PWM), J12.pin4
  N5: U1.D4, J12.pin5
  N6: U1.VCC, U1.AVCC, U1.AREF, U2.output_voltage, C1.1, J16.pin2, J14.pin2
  N7: U1.XLAT1, Y1.0
  N8: U1.XLAT2, Y1.pin_1
  N9: U1.D5_(PWM), J13.pin1
  N10: U1.D6_(PWM), J13.pin2
  N11: U1.D7, J13.pin3
  N12: U1.D8, J13.pin4
  N13: U1.D9_(PWM), J11.pin5
  N14: U1.D10_(PWM), J11.pin4
  N15: U1.D11_(PWM), J11.pin3
  N16: U1.D12, J11.pin2
  N17: U1.D13, LED1.anode, J11.pin1
  N18: U1.A0, J10.pin6
  N19: U1.A1, J10.pin5
  N20: U1.A2, J10.pin4
  N21: U1.A3, J10.pin3
  N22: U1.A4, J10.pin2
  N23: U1.A5, J10.pin1
  N24: U2.input_voltage, Power_plug1.VCC, J9.pin2
  N25: LED1.cathode, R1.Pin_1

notes:
  -
  +
  9V DC
  A
  1
  2
  3
  4
  5
  0
  D
  10
  11
  12
  13
  9
  8
  7
  6
  5V out
  TX
  RX
  5V in
