# Fritzing sketch bi_color_led_and_resistor_smd (saved by Fritzing 0.8.7b)
circuit board: 0.635cm x 0.904861cm
breadboards: 1

parts:
  Relay_pins9 = female pin header, 2 pins [form="♀ (female)"]
  R1 = Resistor [tolerance=±5% resistance=220 package="0603 [SMD]"]
  LED1 = smd LED [color="Red (633nm)" package="0603 [SMD]"]

nets:
  N1: Relay_pins9.pin1, R1.Pin_0
  N2: Relay_pins9.pin2, LED1.cathode
  N3: R1.Pin_1, LED1.anode

notes:
  - +
  220
