# Fritzing sketch button (saved by Fritzing 0.8.7b)
circuit board: 1.8572cm x 1.36824cm
breadboards: 1

parts:
  S1 = Pushbutton [package="[THT]"]
  R1 = Resistor [tolerance=±5% resistance=10k package=THT]
  JP1 = Header 3 [package=molex-1x3_lock]

nets:
  N1: S1.Pin_1, S1.Pin_2, R1.Pin_1, JP1.3
  N2: S1.Pin_3, S1.Pin_4, JP1.1
  N3: R1.Pin_0, JP1.2

notes:
  GND
  +5V
  Data
