# Fritzing sketch button_v2_larger_button (saved by Fritzing 0.8.7b)
circuit board: 2.82146cm x 1.35883cm
breadboards: 1

parts:
  1k = Resistor [tolerance=±5% resistance=10k package=THT]
  S3 = SWITCH-MOMENTARY-2 [package=tactile-pth-12mm]
  JP2 = Header 3 [package=molex-1x3_lock]

nets:
  N1: 1k.Pin_0, JP2.2
  N2: 1k.Pin_1, S3.3
  N3: S3.2, JP2.3
  N4: S3.4, JP2.1

notes:
  GND
  +5V
  Data
  12mm Button

custom parts:
  SWITCH-MOMENTARY-2: Various NO switches- pushbuttons, reed, etc
