# Fritzing sketch diy_proto_board_v2 (saved by Fritzing 0.8.7b)
circuit board: 4.21435cm x 2.62226cm
breadboards: 1

parts:
  J64 = male pin header, 8 pins [form="♂ (male)"]
  J59 = male pin header, 8 pins [form="♂ (male)"]
  J65 = male pin header, 8 pins [form="♂ (male)"]
  J66 = male pin header, 8 pins [form="♂ (male)"]
  J68 = male pin header, 8 pins [form="♂ (male)"]
  J69 = male pin header, 8 pins [form="♂ (male)"]
  J70 = male pin header, 8 pins [form="♂ (male)"]
  J72 = male pin header, 8 pins [form="♂ (male)"]
  J73 = male pin header, 8 pins [form="♂ (male)"]
  J74 = male pin header, 8 pins [form="♂ (male)"]
  J75 = male pin header, 8 pins [form="♂ (male)"]
  J76 = male pin header, 8 pins [form="♂ (male)"]
  J77 = male pin header, 8 pins [form="♂ (male)"]
  J78 = male pin header, 8 pins [form="♂ (male)"]
  J79 = male pin header, 8 pins [form="♂ (male)"]
  J71 = male pin header, 8 pins [form="♂ (male)"]

nets:
  N1: J64.pin1, J64.pin2, J64.pin3, J64.pin4, J64.pin5, J64.pin6
  N2: J64.pin7, J59.pin7, J65.pin7, J66.pin7, J68.pin7, J69.pin7, J70.pin7, J71.pin7
  N3: J64.pin8, J59.pin8, J65.pin8, J66.pin8, J68.pin8, J69.pin8, J70.pin8, J71.pin8
  N4: J59.pin1, J59.pin2, J59.pin3, J59.pin4, J59.pin5, J59.pin6
  N5: J65.pin1, J65.pin2, J65.pin3, J65.pin4, J65.pin5, J65.pin6
  N6: J66.pin1, J66.pin2, J66.pin3, J66.pin4, J66.pin5, J66.pin6
  N7: J68.pin1, J68.pin2, J68.pin3, J68.pin4, J68.pin5, J68.pin6
  N8: J69.pin1, J69.pin2, J69.pin3, J69.pin4, J69.pin5, J69.pin6
  N9: J70.pin1, J70.pin2, J70.pin3, J70.pin4, J70.pin5, J70.pin6
  N10: J72.pin1, J72.pin2, J72.pin3, J72.pin4, J72.pin5, J72.pin6
  N11: J72.pin7, J73.pin7, J74.pin7, J75.pin7, J76.pin7, J77.pin7, J78.pin7, J79.pin7
  N12: J72.pin8, J73.pin8, J74.pin8, J75.pin8, J76.pin8, J77.pin8, J78.pin8, J79.pin8
  N13: J73.pin1, J73.pin2, J73.pin3, J73.pin4, J73.pin5, J73.pin6
  N14: J74.pin1, J74.pin2, J74.pin3, J74.pin4, J74.pin5, J74.pin6
  N15: J75.pin1, J75.pin2, J75.pin3, J75.pin4, J75.pin5, J75.pin6
  N16: J76.pin1, J76.pin2, J76.pin3, J76.pin4, J76.pin5, J76.pin6
  N17: J77.pin1, J77.pin2, J77.pin3, J77.pin4, J77.pin5, J77.pin6
  N18: J78.pin1, J78.pin2, J78.pin3, J78.pin4, J78.pin5, J78.pin6
  N19: J79.pin1, J79.pin2, J79.pin3, J79.pin4, J79.pin5, J79.pin6
  N20: J71.pin1, J71.pin2, J71.pin3, J71.pin4, J71.pin5, J71.pin6

notes:
  + -
