# Fritzing sketch glados_rf266_door_rev2 (saved by Fritzing 0.8.7b)
circuit board: 6.09023cm x 3.78578cm
breadboards: 1

parts:
  Relay_pins1 = female pin header, 2 pins [form="♀ (female)"]
  C1 = Electrolytic Capacitor [capacitance=10μF package="100 mil [THT, electrolytic]"]
  C2 = Electrolytic Capacitor [capacitance=10μF package="100 mil [THT, electrolytic]"]
  Relay_pins2 = female pin header, 2 pins [form="♀ (female)"]
  Relay_pins3 = female pin header, 3 pins [form="♀ (female)"]
  Relay_pins4 = female pin header, 3 pins [form="♀ (female)"]
  J18 = female alternating pin header, 4 pins [form="♀ (female)"]
  U1 = Voltage Regulator - 5V [package="TO220 [THT]"]
  C3 = Electrolytic Capacitor [capacitance=10μF package="100 mil [THT, electrolytic]"]
  C4 = Electrolytic Capacitor [capacitance=10μF package="100 mil [THT, electrolytic]"]
  Relay_pins8 = female pin header, 2 pins [form="♀ (female)"]
  Relay_pins7 = female pin header, 3 pins [form="♀ (female)"]
  J16 = female alternating pin header, 6 pins [form="♀ (female)"]
  Relay_pins6 = female pin header, 3 pins [form="♀ (female)"]
  Relay_pins5 = female pin header, 3 pins [form="♀ (female)"]
  J14 = female pin header, 10 pins [form="♀ (female)"]
  Relay_pins9 = female pin header, 3 pins [form="♀ (female)"]
  J13 = female pin header, 10 pins [form="♀ (female)"]

nets:
  N1: Relay_pins1.pin1, C2.+, Relay_pins2.pin2, U1.input_voltage, C4.+, Relay_pins9.pin1
  N2: Relay_pins1.pin2, C1.-, C2.-, Relay_pins2.pin1, Relay_pins3.pin2, Relay_pins4.pin2, U1.GND, C3.-, C4.-, Relay_pins8.pin1, Relay_pins7.pin2, Relay_pins6.pin2, Relay_pins5.pin2, Relay_pins9.pin3, J13.pin10
  N3: C1.+, Relay_pins3.pin1, Relay_pins4.pin1, Relay_pins7.pin1, Relay_pins6.pin1, Relay_pins5.pin1, Relay_pins9.pin2, J13.pin1
  N4: Relay_pins3.pin3, J13.pin9
  N5: Relay_pins4.pin3, J13.pin3
  N6: J18.pin1, J13.pin4
  N7: J18.pin2, J13.pin5
  N8: J18.pin3, J13.pin6
  N9: J18.pin4, J13.pin7
  N10: U1.output_voltage, C3.+, Relay_pins8.pin2
  N11: Relay_pins7.pin3, J14.pin8
  N12: J16.pin1, J14.pin1
  N13: J16.pin2, J14.pin2
  N14: J16.pin3, J14.pin3
  N15: J16.pin4, J14.pin4
  N16: J16.pin5, J14.pin5
  N17: J16.pin6, J14.pin6
  N18: Relay_pins6.pin3, J14.pin9
  N19: Relay_pins5.pin3, J14.pin10

notes:
  1    3.3V
  12v IN
  + -
  3.3V Regulator
  10uF
  2   IO_11 TX
  3   IO_10 RX
  4 IO_21  PWM
  5 RESET
  6 IO_20   PWM
  7 IO_19   PWM
  9    IO_9 SDA
  10 | GND
  IO_15      11
  CTS IO_12   12
  IO_15 | 11
  SCL IO_8   13
  PWM        IO_37 15
  RTS        IO_23 16
  ADC7       IO_17 17
  ADC6       MOSI 18
  ADC5   SCLK 19
  ADC4   MISO 20
  12v OUT
  + - S
  5V Regulator
  IN GND OUT
  5V OUT
  GND Vout Vin
