# Fritzing sketch glados_rf266_door_rev3 (saved by Fritzing 0.8.7b)
circuit board: 4.61173cm x 3.59945cm
breadboards: 1

parts:
  Relay_pins1 = female pin header, 2 pins [form="♀ (female)"]
  C1 = Electrolytic Capacitor [capacitance=10μF package="100 mil [THT, electrolytic]"]
  C2 = Electrolytic Capacitor [capacitance=10μF package="100 mil [THT, electrolytic]"]
  Relay_pins2 = female pin header, 2 pins [form="♀ (female)"]
  U1 = Voltage Regulator - 5V [package="TO220 [THT]"]
  C3 = Electrolytic Capacitor [capacitance=10μF package="100 mil [THT, electrolytic]"]
  C4 = Electrolytic Capacitor [capacitance=10μF package="100 mil [THT, electrolytic]"]
  Relay_pins8 = female pin header, 2 pins [form="♀ (female)"]
  Relay_pins7 = female pin header, 3 pins [form="♀ (female)"]
  J14 = female pin header, 10 pins [form="♀ (female)"]
  Relay_pins9 = female pin header, 3 pins [form="♀ (female)"]
  Relay_pins3 = female pin header, 3 pins [form="♀ (female)"]
  J18 = female alternating pin header, 4 pins [form="♀ (female)"]
  Relay_pins10 = female pin header, 2 pins [form="♀ (female)"]
  Relay_pins4 = female pin header, 3 pins [form="♀ (female)"]
  Relay_pins11 = female pin header, 3 pins [form="♀ (female)"]
  Relay_pins12 = female pin header, 3 pins [form="♀ (female)"]
  Relay_pins13 = female pin header, 2 pins [form="♀ (female)"]
  J13 = female pin header, 10 pins [form="♀ (female)"]
  J16 = female alternating pin header, 3 pins [form="♀ (female)"]

nets:
  N1: Relay_pins1.pin1, C2.+, Relay_pins2.pin2, U1.input_voltage, C4.+, Relay_pins9.pin1
  N2: Relay_pins1.pin2, C1.-, C2.-, Relay_pins2.pin1, U1.GND, C3.-, C4.-, Relay_pins8.pin1, Relay_pins7.pin2, Relay_pins9.pin3, Relay_pins3.pin2, Relay_pins4.pin2, Relay_pins11.pin2, Relay_pins12.pin2, Relay_pins13.pin2, J13.pin10
  N3: C1.+, Relay_pins7.pin1, Relay_pins9.pin2, Relay_pins3.pin1, Relay_pins4.pin1, Relay_pins11.pin3, Relay_pins12.pin3, J13.pin1
  N4: U1.output_voltage, C3.+, Relay_pins8.pin2
  N5: Relay_pins7.pin3, J14.pin3
  N6: J14.pin1, Relay_pins10.pin2
  N7: J14.pin2, Relay_pins10.pin1
  N8: J14.pin4, J16.pin1
  N9: J14.pin5, J16.pin2
  N10: J14.pin6, J16.pin3
  N11: J14.pin8, Relay_pins13.pin1
  N12: J14.pin9, Relay_pins12.pin1
  N13: J14.pin10, Relay_pins11.pin1
  N14: Relay_pins3.pin3, J13.pin9
  N15: J18.pin1, J13.pin4
  N16: J18.pin2, J13.pin5
  N17: J18.pin3, J13.pin6
  N18: J18.pin4, J13.pin7
  N19: Relay_pins4.pin3, J13.pin3

notes:
  1 3.3V
  12v IN
  + -
  3.3V Regulator
  10uF
  IO_11 TX
  IO_10 RX
  4 IO_21 PWM
  5 RESET
  6 IO_20 PWM
  10 GND
  IO_15 | 11
  12v OUT
  + - S
  5V Regulator
  IN GND OUT
  5V OUT
  GND Vout Vin
  FOB
  DOOR
  9    IO_9 SDA
  7 IO_19 PWM
  IO_15 11
  CTS IO_12 12
  SCL IO_8 13
  PWM IO_37 15
  RTS IO_23 16
  ADC7 IO_17 17
  ADC6 MOSI 18
  ADC5 SCLK 19
  ADC4 MISO 20
  Green Red
  LED
  Exit Button
  DoorBell Button
  keypad
  -
  buzzer
  RX
