# Fritzing sketch led_tht_resistor_smd (saved by Fritzing 0.8.7b)
circuit board: 0.76651cm x 1.25004cm
breadboards: 1

parts:
  LED1 = LED - 5mm [color="Red (633nm)" package="5 mm [THT]"]
  Relay_pins9 = female pin header, 2 pins [form="♀ (female)"]
  R1 = Resistor [tolerance=±5% resistance=220 package="0603 [SMD]"]

nets:
  N1: LED1.cathode, Relay_pins9.pin2
  N2: LED1.anode, R1.Pin_1
  N3: Relay_pins9.pin1, R1.Pin_0

notes:
  - +
  220
