# Fritzing sketch led_tht_rev1 (saved by Fritzing 0.8.7b)
circuit board: 1.00548cm x 1.36953cm
breadboards: 1

parts:
  LED1 = LED - 5mm [color="Red (633nm)" package="5 mm [THT]"]
  R1 = Resistor [tolerance=±5% resistance=220 package=THT]
  Relay_pins9 = female pin header, 2 pins [form="♀ (female)"]

nets:
  N1: LED1.cathode, Relay_pins9.pin2
  N2: LED1.anode, R1.Pin_1
  N3: R1.Pin_0, Relay_pins9.pin1

notes:
  - +
  220
