# Fritzing sketch nrf24l01_8_pin_socket_v1 (saved by Fritzing 0.9.0b)
circuit board: 2.33038cm x 2.14828cm
breadboards: 1

parts:
  J18 = double row female pin header, 8 pins [form="♀ (female)"]
  J19 = female pin header, 8 pins [form="♀ (female)"]

nets:
  N1: J18.pin1, J19.pin4
  N2: J18.pin2, J19.pin3
  N3: J18.pin3, J19.pin2
  N4: J18.pin4, J19.pin1
  N5: J18.pin5, J19.pin8
  N6: J18.pin6, J19.pin7
  N7: J18.pin7, J19.pin6
  N8: J18.pin8, J19.pin5

notes:
  GND
  SCK
  3V3
  CE
  CSN
  MOSI
  MISO
  IRQ
