# Fritzing sketch test_membrane (saved by Fritzing 0.8.7b)
circuit board: 2.45253cm x 2.61157cm
breadboards: 1

parts:
  JP2 = Header 3 [package=molex-1x3_lock]
  R7 = Resistor [tolerance=±5% resistance=4.7k package=THT]
  R8 = Resistor [tolerance=±5% resistance=4.7k package=THT]
  R9 = Resistor [tolerance=±5% resistance=4.7k package=THT]
  R10 = Resistor [tolerance=±5% resistance=1k package=THT]
  R11 = Resistor [tolerance=±5% resistance=1k package=THT]
  R12 = Resistor [tolerance=±5% resistance=1k package=THT]
  J1 = female pin header, 7 pins [form="♀ (female)"]

nets:
  N1: JP2.1, R10.Pin_0, R11.Pin_0, J1.pin7
  N2: JP2.2, R7.Pin_0, J1.pin1
  N3: JP2.3, R10.Pin_1
  N4: R7.Pin_1, R8.Pin_0, J1.pin2
  N5: R8.Pin_1, R9.Pin_0, J1.pin3
  N6: R9.Pin_1, J1.pin4
  N7: R11.Pin_1, R12.Pin_0, J1.pin6
  N8: R12.Pin_1, J1.pin5

notes:
  PIN
  5V
  GND
  1
  7
