# Fritzing sketch ws812_circuits (saved by Fritzing 0.9.0b)
circuit board: 1.95594cm x 0.930688cm
breadboards: 1

parts:
  J1 = female pin header, 3 pins [form="♀ (female)"]
  J2 = female pin header, 3 pins [form="♀ (female)"]
  J3 = female pin header, 1 pin [form="♀ (female)"]
  RGB_SMD_LED1 = SMD RGB LED (WS2812) [package=5050]
  150R = Resistor [tolerance=±5% resistance=150 package="0603 [SMD]"]
  C1 = Capacitor [package=0603-cap]

nets:
  N1: J1.pin1, J2.pin1, RGB_SMD_LED1.VDD, 150R.Pin_1
  N2: J1.pin2, RGB_SMD_LED1.DIn
  N3: J1.pin3, J2.pin3, RGB_SMD_LED1.VSS, C1.2
  N4: J2.pin2, RGB_SMD_LED1.DOut
  N5: J3.pin1, RGB_SMD_LED1.VCC, 150R.Pin_0, C1.1

notes:
  DI
  GND
  DO
  5V+
  *
  0.1uF
  150R
