# Fritzing sketch ws812_strip_10_v1 (saved by Fritzing 0.9.0b)
circuit board: 10.2533cm x 0.95891cm
breadboards: 1

parts:
  J1 = female pin header, 3 pins [form="♀ (female)"]
  J3 = female pin header, 1 pin [form="♀ (female)"]
  RGB_SMD_LED1 = SMD RGB LED (WS2812) [package=5050]
  150R = Resistor [tolerance=±5% resistance=150 package="0603 [SMD]"]
  C1 = Capacitor [package=0603-cap]
  J4 = female pin header, 1 pin [form="♀ (female)"]
  150R1 = Resistor [tolerance=±5% resistance=150 package="0603 [SMD]"]
  C2 = Capacitor [package=0603-cap]
  RGB_SMD_LED2 = SMD RGB LED (WS2812) [package=5050]
  RGB_SMD_LED3 = SMD RGB LED (WS2812) [package=5050]
  C4 = Capacitor [package=0603-cap]
  J6 = female pin header, 1 pin [form="♀ (female)"]
  J5 = female pin header, 1 pin [form="♀ (female)"]
  150R2 = Resistor [tolerance=±5% resistance=150 package="0603 [SMD]"]
  RGB_SMD_LED4 = SMD RGB LED (WS2812) [package=5050]
  150R3 = Resistor [tolerance=±5% resistance=150 package="0603 [SMD]"]
  C3 = Capacitor [package=0603-cap]
  J7 = female pin header, 1 pin [form="♀ (female)"]
  J8 = female pin header, 1 pin [form="♀ (female)"]
  J9 = female pin header, 1 pin [form="♀ (female)"]
  150R4 = Resistor [tolerance=±5% resistance=150 package="0603 [SMD]"]
  150R5 = Resistor [tolerance=±5% resistance=150 package="0603 [SMD]"]
  150R6 = Resistor [tolerance=±5% resistance=150 package="0603 [SMD]"]
  C5 = Capacitor [package=0603-cap]
  C6 = Capacitor [package=0603-cap]
  C7 = Capacitor [package=0603-cap]
  RGB_SMD_LED5 = SMD RGB LED (WS2812) [package=5050]
  RGB_SMD_LED6 = SMD RGB LED (WS2812) [package=5050]
  RGB_SMD_LED7 = SMD RGB LED (WS2812) [package=5050]
  J10 = female pin header, 1 pin [form="♀ (female)"]
  J11 = female pin header, 1 pin [form="♀ (female)"]
  J12 = female pin header, 1 pin [form="♀ (female)"]
  150R7 = Resistor [tolerance=±5% resistance=150 package="0603 [SMD]"]
  150R8 = Resistor [tolerance=±5% resistance=150 package="0603 [SMD]"]
  150R9 = Resistor [tolerance=±5% resistance=150 package="0603 [SMD]"]
  C8 = Capacitor [package=0603-cap]
  C9 = Capacitor [package=0603-cap]
  C10 = Capacitor [package=0603-cap]
  RGB_SMD_LED8 = SMD RGB LED (WS2812) [package=5050]
  RGB_SMD_LED9 = SMD RGB LED (WS2812) [package=5050]
  RGB_SMD_LED10 = SMD RGB LED (WS2812) [package=5050]
  J13 = female pin header, 3 pins [form="♀ (female)"]

nets:
  N1: J1.pin1, RGB_SMD_LED1.VDD, 150R.Pin_1, 150R1.Pin_1, 150R2.Pin_1
  N2: J1.pin2, RGB_SMD_LED1.DIn
  VSS: J1.pin3, RGB_SMD_LED1.VSS, C1.2, C2.2, RGB_SMD_LED2.VSS, RGB_SMD_LED3.VSS, C4.2, RGB_SMD_LED4.VSS, C3.2, C5.2, C6.2, C7.2, RGB_SMD_LED5.VSS, RGB_SMD_LED6.VSS, RGB_SMD_LED7.VSS, C8.2, C9.2, C10.2, RGB_SMD_LED8.VSS, RGB_SMD_LED9.VSS, RGB_SMD_LED10.VSS, J13.pin3
  N3: J3.pin1, RGB_SMD_LED1.VCC, 150R.Pin_0, C1.1
  N4: RGB_SMD_LED1.DOut, RGB_SMD_LED2.DIn
  VCC: J4.pin1, 150R1.Pin_0, C2.1, RGB_SMD_LED2.VCC, RGB_SMD_LED2.VDD
  N5: RGB_SMD_LED2.DOut, RGB_SMD_LED3.DIn
  N6: RGB_SMD_LED3.DOut, RGB_SMD_LED4.DIn
  VCC_2: RGB_SMD_LED3.VCC, RGB_SMD_LED3.VDD, J5.pin1, 150R2.Pin_0, 150R3.Pin_1, C3.1
  VCC_3: C4.1, J6.pin1, RGB_SMD_LED4.VCC, RGB_SMD_LED4.VDD, 150R3.Pin_0, 150R6.Pin_1
  N7: RGB_SMD_LED4.DOut, RGB_SMD_LED6.DIn
  VCC_4: J7.pin1, 150R5.Pin_1, 150R6.Pin_0, C5.1, RGB_SMD_LED6.VCC, RGB_SMD_LED6.VDD
  VCC_5: J8.pin1, 150R4.Pin_0, C7.1, RGB_SMD_LED7.VCC, RGB_SMD_LED7.VDD, 150R7.Pin_1
  VCC_6: J9.pin1, 150R4.Pin_1, 150R5.Pin_0, C6.1, RGB_SMD_LED5.VCC, RGB_SMD_LED5.VDD
  N8: RGB_SMD_LED5.DOut, RGB_SMD_LED7.DIn
  N9: RGB_SMD_LED5.DIn, RGB_SMD_LED6.DOut
  N10: RGB_SMD_LED7.DOut, RGB_SMD_LED9.DIn
  VCC_7: J10.pin1, 150R8.Pin_0, 150R9.Pin_1, C9.1, RGB_SMD_LED8.VCC, RGB_SMD_LED8.VDD
  VCC_8: J11.pin1, 150R9.Pin_0, C10.1, RGB_SMD_LED10.VCC, RGB_SMD_LED10.VDD, J13.pin1
  VCC_9: J12.pin1, 150R7.Pin_0, 150R8.Pin_1, C8.1, RGB_SMD_LED9.VCC, RGB_SMD_LED9.VDD
  N11: RGB_SMD_LED8.DOut, RGB_SMD_LED10.DIn
  N12: RGB_SMD_LED8.DIn, RGB_SMD_LED9.DOut
  N13: RGB_SMD_LED10.DOut, J13.pin2

notes:
  DI
  GND
  5V+
  *
  0.1uF
  150R
  DO
