# Fritzing sketch ws812_strip_16_v1 (saved by Fritzing 0.9.0b)
circuit board: 16.1235cm x 1.00595cm
breadboards: 1

parts:
  RGB_SMD_LED11 = SMD RGB LED (WS2812) [package=5050]
  J14 = female pin header, 3 pins [form="♀ (female)"]
  150R10 = Resistor [tolerance=±5% resistance=150 package="0603 [SMD]"]
  J15 = female pin header, 1 pin [form="♀ (female)"]
  C12 = Capacitor [package=0603-cap]
  J16 = female pin header, 1 pin [form="♀ (female)"]
  150R11 = Resistor [tolerance=±5% resistance=150 package="0603 [SMD]"]
  C13 = Capacitor [package=0603-cap]
  RGB_SMD_LED12 = SMD RGB LED (WS2812) [package=5050]
  J17 = female pin header, 1 pin [form="♀ (female)"]
  150R12 = Resistor [tolerance=±5% resistance=150 package="0603 [SMD]"]
  C14 = Capacitor [package=0603-cap]
  RGB_SMD_LED13 = SMD RGB LED (WS2812) [package=5050]
  J18 = female pin header, 1 pin [form="♀ (female)"]
  J19 = female pin header, 1 pin [form="♀ (female)"]
  J20 = female pin header, 1 pin [form="♀ (female)"]
  150R13 = Resistor [tolerance=±5% resistance=150 package="0603 [SMD]"]
  150R14 = Resistor [tolerance=±5% resistance=150 package="0603 [SMD]"]
  150R15 = Resistor [tolerance=±5% resistance=150 package="0603 [SMD]"]
  C15 = Capacitor [package=0603-cap]
  C16 = Capacitor [package=0603-cap]
  C17 = Capacitor [package=0603-cap]
  RGB_SMD_LED14 = SMD RGB LED (WS2812) [package=5050]
  RGB_SMD_LED15 = SMD RGB LED (WS2812) [package=5050]
  RGB_SMD_LED16 = SMD RGB LED (WS2812) [package=5050]
  J21 = female pin header, 1 pin [form="♀ (female)"]
  J22 = female pin header, 1 pin [form="♀ (female)"]
  J23 = female pin header, 1 pin [form="♀ (female)"]
  150R16 = Resistor [tolerance=±5% resistance=150 package="0603 [SMD]"]
  150R17 = Resistor [tolerance=±5% resistance=150 package="0603 [SMD]"]
  150R18 = Resistor [tolerance=±5% resistance=150 package="0603 [SMD]"]
  C18 = Capacitor [package=0603-cap]
  C19 = Capacitor [package=0603-cap]
  C20 = Capacitor [package=0603-cap]
  RGB_SMD_LED17 = SMD RGB LED (WS2812) [package=5050]
  RGB_SMD_LED18 = SMD RGB LED (WS2812) [package=5050]
  RGB_SMD_LED19 = SMD RGB LED (WS2812) [package=5050]
  J24 = female pin header, 1 pin [form="♀ (female)"]
  J25 = female pin header, 1 pin [form="♀ (female)"]
  J26 = female pin header, 1 pin [form="♀ (female)"]
  150R19 = Resistor [tolerance=±5% resistance=150 package="0603 [SMD]"]
  150R20 = Resistor [tolerance=±5% resistance=150 package="0603 [SMD]"]
  150R21 = Resistor [tolerance=±5% resistance=150 package="0603 [SMD]"]
  C21 = Capacitor [package=0603-cap]
  C22 = Capacitor [package=0603-cap]
  C23 = Capacitor [package=0603-cap]
  RGB_SMD_LED20 = SMD RGB LED (WS2812) [package=5050]
  RGB_SMD_LED21 = SMD RGB LED (WS2812) [package=5050]
  RGB_SMD_LED22 = SMD RGB LED (WS2812) [package=5050]
  J27 = female pin header, 1 pin [form="♀ (female)"]
  J28 = female pin header, 1 pin [form="♀ (female)"]
  J29 = female pin header, 1 pin [form="♀ (female)"]
  150R22 = Resistor [tolerance=±5% resistance=150 package="0603 [SMD]"]
  150R23 = Resistor [tolerance=±5% resistance=150 package="0603 [SMD]"]
  150R24 = Resistor [tolerance=±5% resistance=150 package="0603 [SMD]"]
  C24 = Capacitor [package=0603-cap]
  C25 = Capacitor [package=0603-cap]
  C26 = Capacitor [package=0603-cap]
  RGB_SMD_LED23 = SMD RGB LED (WS2812) [package=5050]
  RGB_SMD_LED24 = SMD RGB LED (WS2812) [package=5050]
  RGB_SMD_LED25 = SMD RGB LED (WS2812) [package=5050]
  J30 = female pin header, 1 pin [form="♀ (female)"]
  150R27 = Resistor [tolerance=±5% resistance=150 package="0603 [SMD]"]
  C28 = Capacitor [package=0603-cap]
  RGB_SMD_LED27 = SMD RGB LED (WS2812) [package=5050]
  J31 = female pin header, 3 pins [form="♀ (female)"]

nets:
  N1: RGB_SMD_LED11.DOut, RGB_SMD_LED12.DIn
  N2: RGB_SMD_LED11.DIn, J14.pin2
  VCC: RGB_SMD_LED11.VCC, RGB_SMD_LED11.VDD, J14.pin1, 150R10.Pin_1, J15.pin1, J16.pin1, 150R11.Pin_1, RGB_SMD_LED12.VCC, RGB_SMD_LED12.VDD, J17.pin1, 150R12.Pin_1, RGB_SMD_LED13.VCC, RGB_SMD_LED13.VDD, J18.pin1, J19.pin1, J20.pin1, 150R13.Pin_1, 150R14.Pin_1, 150R15.Pin_1, RGB_SMD_LED14.VCC, RGB_SMD_LED14.VDD, RGB_SMD_LED15.VCC, RGB_SMD_LED15.VDD, RGB_SMD_LED16.VCC, RGB_SMD_LED16.VDD, J21.pin1, J22.pin1, J23.pin1, 150R16.Pin_1, 150R17.Pin_1, 150R18.Pin_1, RGB_SMD_LED17.VCC, RGB_SMD_LED17.VDD, RGB_SMD_LED18.VCC, RGB_SMD_LED18.VDD, RGB_SMD_LED19.VCC, RGB_SMD_LED19.VDD, J24.pin1, J25.pin1, J26.pin1, 150R19.Pin_1, 150R20.Pin_1, 150R21.Pin_1, RGB_SMD_LED20.VCC, RGB_SMD_LED20.VDD, RGB_SMD_LED21.VCC, RGB_SMD_LED21.VDD, RGB_SMD_LED22.VCC, RGB_SMD_LED22.VDD, J27.pin1, J28.pin1, J29.pin1, 150R22.Pin_1, 150R23.Pin_1, 150R24.Pin_1, RGB_SMD_LED23.VCC, RGB_SMD_LED23.VDD, RGB_SMD_LED24.VCC, RGB_SMD_LED24.VDD, RGB_SMD_LED25.VCC, RGB_SMD_LED25.VDD, J30.pin1, 150R27.Pin_1, RGB_SMD_LED27.VCC, RGB_SMD_LED27.VDD, J31.pin1
  VSS: RGB_SMD_LED11.VSS, J14.pin3, C12.2, C13.2, RGB_SMD_LED12.VSS, C14.2, RGB_SMD_LED13.VSS, C15.2, C16.2, C17.2, RGB_SMD_LED14.VSS, RGB_SMD_LED15.VSS, RGB_SMD_LED16.VSS, C18.2, C19.2, C20.2, RGB_SMD_LED17.VSS, RGB_SMD_LED18.VSS, RGB_SMD_LED19.VSS, C21.2, C22.2, C23.2, RGB_SMD_LED20.VSS, RGB_SMD_LED21.VSS, RGB_SMD_LED22.VSS, C24.2, C25.2, C26.2, RGB_SMD_LED23.VSS, RGB_SMD_LED24.VSS, RGB_SMD_LED25.VSS, C28.2, RGB_SMD_LED27.VSS, J31.pin3
  N3: 150R10.Pin_0, C12.1
  N4: 150R11.Pin_0, C13.1
  N5: RGB_SMD_LED12.DOut, RGB_SMD_LED13.DIn
  N6: 150R12.Pin_0, C14.1
  N7: RGB_SMD_LED13.DOut, RGB_SMD_LED15.DIn
  N8: 150R13.Pin_0, C15.1
  N9: 150R14.Pin_0, C17.1
  N10: 150R15.Pin_0, C16.1
  N11: RGB_SMD_LED14.DOut, RGB_SMD_LED16.DIn
  N12: RGB_SMD_LED14.DIn, RGB_SMD_LED15.DOut
  N13: RGB_SMD_LED16.DOut, RGB_SMD_LED18.DIn
  N14: 150R16.Pin_0, C18.1
  N15: 150R17.Pin_0, C20.1
  N16: 150R18.Pin_0, C19.1
  N17: RGB_SMD_LED17.DOut, RGB_SMD_LED19.DIn
  N18: RGB_SMD_LED17.DIn, RGB_SMD_LED18.DOut
  N19: RGB_SMD_LED19.DOut, RGB_SMD_LED21.DIn
  N20: 150R19.Pin_0, C21.1
  N21: 150R20.Pin_0, C23.1
  N22: 150R21.Pin_0, C22.1
  N23: RGB_SMD_LED20.DOut, RGB_SMD_LED22.DIn
  N24: RGB_SMD_LED20.DIn, RGB_SMD_LED21.DOut
  N25: RGB_SMD_LED22.DOut, RGB_SMD_LED24.DIn
  N26: 150R22.Pin_0, C24.1
  N27: 150R23.Pin_0, C26.1
  N28: 150R24.Pin_0, C25.1
  N29: RGB_SMD_LED23.DOut, RGB_SMD_LED25.DIn
  N30: RGB_SMD_LED23.DIn, RGB_SMD_LED24.DOut
  N31: RGB_SMD_LED25.DOut, RGB_SMD_LED27.DIn
  N32: 150R27.Pin_0, C28.1
  N33: RGB_SMD_LED27.DOut, J31.pin2

notes:
  5V+
  *
  DO
  GND
  DI
